# Fritzing sketch MIDI controller (saved by Fritzing 0.9.4)
breadboards: 2

parts:
  Part1 = Arduino Leonardo (Rev3b)
  R1 = Rotary Potentiometer (Small) [maximum_resistance=10kΩ package=THT]
  R2 = Rotary Potentiometer (Small) [maximum_resistance=10kΩ package=THT]
  R3 = Rotary Potentiometer (Small) [maximum_resistance=10kΩ package=THT]
  R4 = Rotary Potentiometer (Small) [maximum_resistance=10kΩ package=THT]
  R5 = Rotary Potentiometer (Small) [maximum_resistance=10kΩ package=THT]

nets:
  N1: Part1.5V, R1.leg1, R2.leg1, R3.leg1, R4.leg1, R5.leg1
  N2: Part1.GND, R1.leg2, R2.leg2, R3.leg2, R4.leg2, R5.leg2
  N3: Part1.A0, R4.wiper
  N4: Part1.A1, R5.wiper
  N5: Part1.A2, R2.wiper
  N6: Part1.A3, R3.wiper
  N7: Part1.A4, R1.wiper
